# Fritzing sketch servo-opener (saved by Fritzing 0.9.3b)
breadboards: 1

parts:
  Secondary = Basic Servo
  Primary = Basic Servo
  MKR1000 = Arduino MKR1000

nets:
  GND: Secondary.gnd, Primary.gnd, MKR1000.GND
  VCC: Secondary.vcc, Primary.vcc, MKR1000.5V
  N1: Secondary.pulse, MKR1000.D3_PWM
  N2: Primary.pulse, MKR1000.D2_PWM

custom parts:
  Arduino MKR1000: MKR1000 is a powerful board that combines the functionality of the Zero and the Wi-Fi Shield. It is the ideal solution for makers wanting to design IoT projects with minimal previous experience in networking
